// Logisim project SmartWaterTank (2).circ as structural Verilog: 1 circuit, main circuit main
module main (
  input  L,
  input  M,
  input  F
);

  wire and_1_out, and_2_out, and_3_out, not_1_out, not_2_out, not_3_out, or_1_out;

  not not_1 (not_1_out, L);
  not not_2 (not_2_out, M);
  not not_3 (not_3_out, F);
  and and_1 (and_1_out, not_2_out, L, not_3_out);
  and and_2 (and_2_out, not_1_out, M, not_3_out);
  and and_3 (and_3_out, not_1_out, not_2_out, F);
  LED led_1 (.in(and_1_out));
  or or_1 (or_1_out, and_1_out, and_2_out);
  LED led_2 (.in(and_2_out));
  LED led_3 (.in(and_3_out));
  LED led_4 (.in(or_1_out));
endmodule
